# Fritzing sketch schematic_H (saved by Fritzing 0.9.3b)
breadboards: 1

parts:
  S1 = Pushbutton [package=THT]
  S2 = Pushbutton [package=THT]
  S3 = Pushbutton [package=THT]
  S4 = Pushbutton [package=THT]
  M1 = DC Motor

nets:
  N1: S1.leg0, S3.leg1, M1.pin_2
  5V: S1.leg1, S2.leg1
  N2: S2.leg0, S4.leg1, M1.pin_1
  GND: S3.leg0, S4.leg0
