# Fritzing sketch fritzing_1 (saved by Fritzing 0.9.3b)
breadboards: 1

parts:
  Raspberry_Pi1 = Raspberry Pi B+
  LED1 = LED - 5mm [color="Red (633nm)" package="5 mm [THT]"]
  R3 = Resistor [tolerance=±1% resistance=68 package=THT]

nets:
  N1: Raspberry_Pi1.3v3, LED1.anode
  N2: Raspberry_Pi1.GND, R3.Pin_0
  N3: LED1.cathode, R3.Pin_1
