# Fritzing sketch fritzing_3 (saved by Fritzing 0.9.3b)
breadboards: 1

parts:
  Raspberry_Pi1 = Raspberry Pi B+
  LED1 = RGB LED (com. cathode, rgb) [package="5 mm [THT]"]
  R1 = Resistor [tolerance=±1% resistance=1 package=THT]
  R2 = Resistor [tolerance=±1% resistance=68 package=THT]
  R3 = Resistor [tolerance=±1% resistance=68 package=THT]

nets:
  N1: Raspberry_Pi1.GPIO21, R2.Pin_1
  N2: Raspberry_Pi1.GPIO20, R1.Pin_1
  N3: Raspberry_Pi1.GPIO16, R3.Pin_1
  N4: Raspberry_Pi1.GND, LED1.green_anode
  N5: LED1.red_anode, R3.Pin_0
  N6: LED1.common_cathode, R1.Pin_0
  N7: LED1.blue_anode, R2.Pin_0
