# Fritzing sketch schematic (saved by Fritzing 0.9.3b)
breadboards: 1

parts:
  Raspberry_Pi_1 = Raspberry Pi 3 [part_number=RPI-3-V1.2]
  IC1 = L293DNE [package=THT]
  M1 = DC Motor

nets:
  N1: Raspberry_Pi_1.GND, IC1.0V
  N2: Raspberry_Pi_1.GPIO25, IC1.Enable_2
  N3: Raspberry_Pi_1.GPIO24, IC1.In_3
  N4: Raspberry_Pi_1.GPIO23, IC1.In_4
  N5: Raspberry_Pi_1.5V, IC1.+Vmotor, IC1.+V
  N6: IC1.Out_3_(_Controlled_by_Enable_2_), M1.pin_2
  N7: IC1.Out_4_(_Controlled_by_Enable_2_), M1.pin_1

custom parts:
  L293DNE: L293DNE Motor Driver
