# Fritzing sketch fritzing_2 (saved by Fritzing 0.9.3b)
breadboards: 1

parts:
  Raspberry_Pi1 = Raspberry Pi B+
  LED1 = LED - 5mm [color="Red (633nm)" package="5 mm [THT]"]
  LED2 = LED - 5mm [color="Yellow (595nm)" package="5 mm [THT]"]
  LED3 = LED - 5mm [color="Green (555nm)" package="5 mm [THT]"]
  R1 = Resistor [tolerance=±1% resistance=68 package=THT]
  R2 = Resistor [tolerance=±1% resistance=68 package=THT]
  R3 = Resistor [tolerance=±1% resistance=68 package=THT]
  R4 = Resistor [tolerance=±1% resistance=2.2k package=THT]
  S1 = Pushbutton [package="[THT]"]

nets:
  N1: Raspberry_Pi1.3v3, S1.Pin_3, S1.Pin_4
  N2: Raspberry_Pi1.GPIO21, LED1.anode
  N3: Raspberry_Pi1.GPIO20, LED2.anode
  N4: Raspberry_Pi1.GPIO16, LED3.anode
  N5: Raspberry_Pi1.GND, R1.Pin_0, R2.Pin_0, R3.Pin_0
  N6: Raspberry_Pi1.GPIO14, R4.Pin_1
  N7: LED1.cathode, R1.Pin_1
  N8: LED2.cathode, R2.Pin_1
  N9: LED3.cathode, R3.Pin_1
  N10: R4.Pin_0, S1.Pin_1, S1.Pin_2
